// Digital circuit Control Unit.dig as structural Verilog
module Control_Unit (
  input  [15:0] IR,
  input  CLK,
  input  S,
  input  R,
  input  I,
  input  IEN,
  input  FGI,
  input  FGO,
  input  E,
  input  [15:0] AC,
  input  [15:0] DR,
  input  C_OUT,
  output [6:0] x,
  output S_CLR,
  output I_LD,
  output I_D,
  output R_J,
  output R_K,
  output IEN_J,
  output IEN_K,
  output FGI_K,
  output FGO_K,
  output AR_LD,
  output AR_INR,
  output AR_CLR,
  output MEM_read,
  output MEM_write,
  output PC_LD,
  output PC_INCR,
  output PC_CLR,
  output DR_LD,
  output DR_INCR,
  output AC_LD,
  output AC_INCR,
  output AC_CLR,
  output [6:0] AL_OP,
  output OUTR_LD,
  output IR_LD,
  output TR_LD,
  output [15:0] T,
  output [7:0] D,
  output E_J,
  output E_K
);

  wire AC_0, AC_15, AC_eq_0, and_1_out, and_2_out, and_3_out, and_4_out, and_5_out, and_6_out, and_7_out,
       and_8_out, and_11_out, and_12_out, and_13_out, and_14_out, and_15_out, and_16_out, and_17_out,
       and_21_out, and_22_out, and_23_out, and_24_out, and_25_out, and_30_out, and_31_out, and_32_out,
       and_33_out, and_34_out, and_40_out, and_41_out, and_42_out, and_43_out, and_44_out, and_45_out,
       and_46_out, and_47_out, and_48_out, and_49_out, and_60_out, and_61_out, and_62_out, and_63_out,
       and_64_out, and_65_out, and_67_out, and_68_out, and_69_out, and_70_out, and_71_out, and_72_out,
       and_73_out, and_74_out, and_75_out, and_76_out, and_77_out, and_78_out, and_79_out, and_80_out,
       and_81_out, and_82_out, and_86_out, and_87_out, and_88_out, and_89_out, and_90_out, and_91_out,
       and_92_out, and_93_out, and_94_out, and_95_out, and_96_out, and_97_out, and_98_out, and_99_out,
       and_100_out, and_101_out, DR_eq_0, or_1_out, or_2_out, or_7_out, or_10_out, or_11_out, or_16_out,
       or_17_out, or_21_out, or_22_out, p, r_t;
  wire [3:0] SC_out;

  and and_1 (and_1_out, D[0], T[5]);
  and and_2 (and_2_out, D[1], T[5]);
  and and_3 (and_3_out, D[2], T[5]);
  and and_4 (and_4_out, D[3], T[4]);
  and and_5 (and_5_out, D[4], T[4]);
  and and_6 (and_6_out, D[5], T[5]);
  and and_7 (and_7_out, D[6], T[6]);
  and and_8 (and_8_out, R, T[2]);
  or or_1 (or_1_out, and_1_out, and_2_out, and_3_out, and_4_out, and_5_out, and_6_out, and_7_out, and_8_out, r_t, p);
  BitSelector #(.Selector_Bits(4)) bitselector_1 (.in(AC), .sel(4'b1111), .out(AC_15));
  BitSelector #(.Selector_Bits(4)) bitselector_2 (.in(AC), .sel(4'b0000), .out(AC_0));
  CounterPreset #(.Bits(4)) SC (
    .en(S), .C(CLK), .dir(1'b0), .in(4'b0000), .ld(1'b0), .clr(or_1_out), .out(SC_out));  // open: ovf
  Decoder #(.Selector_Bits(3)) decoder_1 (
    .sel(IR[14:12]), .out_0(D[0]), .out_1(D[1]), .out_2(D[2]), .out_3(D[3]), .out_4(D[4]), .out_5(D[5]),
    .out_6(D[6]), .out_7(D[7]));
  and and_9 (r_t, D[7], ~I, T[3]);  // And
  and and_10 (p, D[7], I, T[3]);
  Comparator #(.Bits(16)) DR_Comparator (.a(DR), .b({16{1'b0}}), .eq(DR_eq_0));  // open: gt, lt
  Comparator #(.Bits(16)) AC_Comparator (.a(AC), .b({16{1'b0}}), .eq(AC_eq_0));  // open: gt, lt
  Decoder #(.Selector_Bits(4)) decoder_2 (
    .sel(SC_out), .out_0(T[0]), .out_1(T[1]), .out_2(T[2]), .out_3(T[3]), .out_4(T[4]), .out_5(T[5]),
    .out_6(T[6]), .out_7(T[7]), .out_8(T[8]), .out_9(T[9]), .out_10(T[10]), .out_11(T[11]), .out_12(T[12]),
    .out_13(T[13]), .out_14(T[14]), .out_15(T[15]));
  and and_11 (and_11_out, D[5], T[4]);
  and and_12 (and_12_out, D[3], T[4]);
  and and_13 (and_13_out, p, IR[10]);
  or or_2 (or_2_out, D[0], D[1], D[2], D[6]);
  and and_14 (and_14_out, D[4], T[4]);
  and and_15 (and_15_out, D[5], T[5]);
  and and_16 (and_16_out, ~R, T[0]);  // And
  and and_17 (and_17_out, R, T[0]);
  and and_18 (x[2], D[6], T[6]);
  or or_3 (x[3], and_12_out, and_13_out);
  and and_19 (x[4], ~R, T[2]);  // And
  and and_20 (x[5], R, T[1]);
  and and_21 (and_21_out, ~R, T[1]);  // And
  and and_22 (and_22_out, ~D[7], I, T[3]);  // And
  and and_23 (and_23_out, or_2_out, T[4]);
  or or_4 (x[0], and_14_out, and_15_out);
  or or_5 (x[1], and_16_out, and_11_out, and_17_out);
  or or_6 (x[6], and_21_out, and_22_out, and_23_out);
  and and_24 (and_24_out, ~T[0], ~T[1], ~T[2]);  // And
  or or_7 (or_7_out, FGI, FGO);
  and and_25 (and_25_out, and_24_out, or_7_out);
  and and_26 (S_CLR, r_t, IR[0]);
  and and_27 (I_LD, ~R, T[2]);  // And
  and and_28 (R_J, and_25_out, IEN);
  and and_29 (R_K, R, T[2]);
  and and_30 (and_30_out, ~R, T[0]);  // And
  and and_31 (and_31_out, ~R, T[1]);  // And
  and and_32 (and_32_out, ~D[7], I, T[3]);  // And
  and and_33 (and_33_out, p, IR[6]);
  and and_34 (and_34_out, R, T[2]);
  and and_35 (IEN_J, p, IR[7]);
  or or_8 (IEN_K, and_33_out, and_34_out);
  and and_36 (FGI_K, p, IR[11]);
  and and_37 (FGO_K, p, IR[10]);
  or or_9 (AR_LD, and_30_out, and_31_out, and_32_out);
  and and_38 (AR_INR, D[5], T[4]);
  and and_39 (AR_CLR, R, T[0]);
  and and_40 (and_40_out, ~D[7], I, T[3]);  // And
  and and_41 (and_41_out, ~R, T[1]);  // And
  and and_42 (and_42_out, D[0], T[4]);
  and and_43 (and_43_out, D[1], T[4]);
  and and_44 (and_44_out, D[2], T[4]);
  and and_45 (and_45_out, D[6], T[4]);
  and and_46 (and_46_out, R, T[1]);
  and and_47 (and_47_out, D[3], T[4]);
  and and_48 (and_48_out, D[5], T[4]);
  and and_49 (and_49_out, D[6], T[6]);
  or or_10 (or_10_out, and_40_out, and_41_out, and_42_out);
  or or_11 (or_11_out, and_43_out, and_44_out, and_45_out);
  or or_12 (MEM_write, and_46_out, and_47_out, and_48_out, and_49_out);
  and and_50 (DR_INCR, D[6], T[5]);
  and and_51 (OUTR_LD, p, IR[10]);
  and and_52 (IR_LD, ~R, T[1]);  // And
  or or_13 (MEM_read, or_10_out, or_11_out);
  and and_53 (AL_OP[0], D[0], T[5]);
  and and_54 (AL_OP[1], D[1], T[5]);
  and and_55 (AL_OP[2], D[2], T[5]);
  and and_56 (AL_OP[3], p, IR[11]);
  and and_57 (AL_OP[4], r_t, IR[9]);
  and and_58 (AL_OP[5], r_t, IR[7]);
  and and_59 (AL_OP[6], r_t, IR[6]);
  and and_60 (and_60_out, D[0], T[4]);
  and and_61 (and_61_out, D[1], T[4]);
  and and_62 (and_62_out, D[2], T[4]);
  and and_63 (and_63_out, D[6], T[4]);
  and and_64 (and_64_out, D[4], T[4]);
  and and_65 (and_65_out, D[5], T[5]);
  or or_14 (DR_LD, and_60_out, and_61_out, and_62_out, and_63_out);
  or or_15 (PC_LD, and_64_out, and_65_out);
  and and_66 (PC_CLR, R, T[1]);
  and and_67 (and_67_out, D[1], C_OUT, T[5]);
  and and_68 (and_68_out, r_t, AC_15, IR[6]);
  and and_69 (and_69_out, r_t, AC_0, IR[7]);
  and and_70 (and_70_out, r_t, ~E, IR[8]);  // And
  and and_71 (and_71_out, r_t, IR[10]);
  and and_72 (and_72_out, D[1], ~C_OUT, T[5]);  // And
  and and_73 (and_73_out, r_t, ~AC_15, IR[6]);  // And
  and and_74 (and_74_out, r_t, ~AC_0, IR[7]);  // And
  and and_75 (and_75_out, r_t, E, IR[8]);
  and and_76 (and_76_out, D[0], T[5]);
  and and_77 (and_77_out, D[1], T[5]);
  and and_78 (and_78_out, D[2], T[5]);
  and and_79 (and_79_out, r_t, IR[7]);
  and and_80 (and_80_out, r_t, IR[6]);
  and and_81 (and_81_out, r_t, IR[9]);
  and and_82 (and_82_out, p, IR[11]);
  and and_83 (AC_INCR, r_t, IR[5]);
  and and_84 (AC_CLR, r_t, IR[11]);
  and and_85 (TR_LD, R, T[0]);
  or or_16 (or_16_out, and_76_out, and_77_out, and_78_out, and_79_out);
  or or_17 (or_17_out, and_80_out, and_81_out, and_82_out);
  or or_18 (E_J, and_67_out, and_68_out, and_69_out, and_70_out);
  or or_19 (E_K, and_71_out, and_72_out, and_73_out, and_74_out, and_75_out);
  or or_20 (AC_LD, or_16_out, or_17_out);
  and and_86 (and_86_out, ~R, T[1]);  // And
  and and_87 (and_87_out, R, T[2]);
  and and_88 (and_88_out, D[6], T[6]);
  and and_89 (and_89_out, r_t, IR[4]);
  and and_90 (and_90_out, r_t, IR[3]);
  and and_91 (and_91_out, r_t, IR[2]);
  and and_92 (and_92_out, r_t, IR[1]);
  and and_93 (and_93_out, p, IR[9]);
  and and_94 (and_94_out, p, IR[8]);
  and and_95 (and_95_out, and_88_out, DR_eq_0);
  and and_96 (and_96_out, and_89_out, ~AC_15);  // And
  and and_97 (and_97_out, and_90_out, AC_15);
  and and_98 (and_98_out, and_91_out, AC_eq_0);
  and and_99 (and_99_out, and_92_out, ~E);  // And
  and and_100 (and_100_out, and_93_out, FGI);
  and and_101 (and_101_out, and_94_out, FGO);
  or or_21 (or_21_out, and_86_out, and_87_out, and_95_out, and_96_out, and_97_out);
  or or_22 (or_22_out, and_98_out, and_99_out, and_100_out, and_101_out);
  or or_23 (PC_INCR, or_21_out, or_22_out);

  assign I_D = IR[15];

  // Other names for the same wires on the sheet: D_0 = D[0]; D_1 = D[1]; D_2 = D[2]; D_3 = D[3]; D_4 = D[4];
  //   D_5 = D[5]; D_6 = D[6]; D_7 = D[7]; Adress[11:0] = IR[11:0]; B_0 = IR[0]; B_1 = IR[1]; B_2 = IR[2]; B_3 = IR[3];
  //   B_4 = IR[4]; B_5 = IR[5]; B_6 = IR[6]; B_7 = IR[7]; B_8 = IR[8]; B_9 = IR[9]; B_10 = IR[10]; B_11 = IR[11];
  //   IR_15 = IR[15]; T_0 = T[0]; T_1 = T[1]; T_2 = T[2]; T_3 = T[3]; T_4 = T[4]; T_5 = T[5]; T_6 = T[6]; T_7 = T[7];
  //   T_8 = T[8]; T_9 = T[9]; T_10 = T[10]; T_11 = T[11]; T_12 = T[12]; T_13 = T[13]; T_14 = T[14]; T_15 = T[15]

  // Notes on the sheet:
  //   IR: default 16
  //   AND
  //   ADD
  //   DR
  //   LDA
  //   CMA
  //   CIR
  //   CIL
endmodule
